// Digital circuit adder_4bit.dig as structural Verilog
module adder_4bit (
  input  A0,
  input  B0,
  input  Cin0,
  input  A1,
  input  B1,
  input  Cin1,
  input  A2,
  input  B2,
  input  Cin2,
  input  A3,
  input  B3,
  input  Cin3,
  output O0,
  output S1,
  output S2,
  output S3,
  output S4
);

  wire and_1_out, and_2_out, and_3_out, and_4_out, and_5_out, and_6_out, and_7_out, and_8_out, xor_1_out,
       xor_2_out, xor_3_out, xor_4_out;

  xor xor_1 (xor_1_out, A0, B0);
  xor xor_2 (xor_2_out, A1, B1);
  xor xor_3 (xor_3_out, A2, B2);
  xor xor_4 (xor_4_out, A3, B3);
  xor xor_5 (O0, xor_1_out, Cin0);
  and and_1 (and_1_out, Cin0, xor_1_out);
  and and_2 (and_2_out, Cin0, A0);
  xor xor_6 (S1, xor_2_out, Cin1);
  and and_3 (and_3_out, Cin1, xor_2_out);
  and and_4 (and_4_out, Cin1, A1);
  xor xor_7 (S2, xor_3_out, Cin2);
  and and_5 (and_5_out, Cin2, xor_3_out);
  and and_6 (and_6_out, Cin2, A2);
  xor xor_8 (S3, xor_4_out, Cin3);
  and and_7 (and_7_out, Cin3, xor_4_out);
  and and_8 (and_8_out, Cin3, A3);
  or or_1 (Cin1, and_1_out, and_2_out);
  or or_2 (Cin2, and_3_out, and_4_out);
  or or_3 (Cin3, and_5_out, and_6_out);
  or or_4 (S4, and_7_out, and_8_out);
endmodule
