// Digital circuit adder_8bit.dig as structural Verilog
module adder_8bit (
);

  wire full_adder_1bit_1_p1, full_adder_1bit_2_p1, full_adder_1bit_3_p1, full_adder_1bit_4_p1,
       full_adder_1bit_5_p1, full_adder_1bit_6_p1, full_adder_1bit_7_p1;

  // full_adder_1bit full_adder_1bit_1: pin names not known; wires that end beside it: full_adder_1bit_1_p1
  // full_adder_1bit full_adder_1bit_2: pin names not known; wires that end beside it: full_adder_1bit_2_p1, full_adder_1bit_1_p1
  // full_adder_1bit full_adder_1bit_3: pin names not known; wires that end beside it: full_adder_1bit_3_p1, full_adder_1bit_2_p1
  // full_adder_1bit full_adder_1bit_4: pin names not known; wires that end beside it: full_adder_1bit_4_p1, full_adder_1bit_3_p1
  // full_adder_1bit full_adder_1bit_5: pin names not known; wires that end beside it: full_adder_1bit_5_p1, full_adder_1bit_4_p1
  // full_adder_1bit full_adder_1bit_6: pin names not known; wires that end beside it: full_adder_1bit_6_p1, full_adder_1bit_5_p1
  // full_adder_1bit full_adder_1bit_7: pin names not known; wires that end beside it: full_adder_1bit_7_p1, full_adder_1bit_6_p1
  // full_adder_1bit full_adder_1bit_8: pin names not known; wires that end beside it: full_adder_1bit_7_p1
endmodule
