// Digital circuit comparator_8bit.dig as structural Verilog
module comparator_8bit (
  input  A0,
  input  A1,
  input  A2,
  input  A3,
  input  A4,
  input  A5,
  input  A6,
  input  A7,
  input  B0,
  input  B1,
  input  B2,
  input  B3,
  input  B4,
  input  B5,
  input  B6,
  input  B7,
  output A__lt__B,
  output A__eq__B,
  output A__gt__B
);

  wire C1_o__eq, C1_o__gt, C1_o__lt, C2_o__eq, C2_o__gt, C2_o__lt, C3_o__eq, C3_o__gt, C3_o__lt, C4_o__eq,
       C4_o__gt, C4_o__lt, C5_o__eq, C5_o__gt, C5_o__lt, C6_o__eq, C6_o__gt, C6_o__lt,
       half_comparator_1bit_1_o__eq, half_comparator_1bit_1_o__gt, half_comparator_1bit_1_o__lt;

  full_comparator_1bit C0 (
    .A(A0), .B(B0), .I__lt(C1_o__lt), .I__eq(C1_o__eq), .I__gt(C1_o__gt), .O__lt(A__lt__B), .O__eq(A__eq__B),
    .O__gt(A__gt__B));
  full_comparator_1bit C1 (
    .A(A1), .B(B1), .I__lt(C2_o__lt), .I__eq(C2_o__eq), .I__gt(C2_o__gt), .O__lt(C1_o__lt), .O__eq(C1_o__eq),
    .O__gt(C1_o__gt));
  full_comparator_1bit C2 (
    .A(A2), .B(B2), .I__lt(C3_o__lt), .I__eq(C3_o__eq), .I__gt(C3_o__gt), .O__lt(C2_o__lt), .O__eq(C2_o__eq),
    .O__gt(C2_o__gt));
  full_comparator_1bit C3 (
    .A(A3), .B(B3), .I__lt(C4_o__lt), .I__eq(C4_o__eq), .I__gt(C4_o__gt), .O__lt(C3_o__lt), .O__eq(C3_o__eq),
    .O__gt(C3_o__gt));
  full_comparator_1bit C4 (
    .A(A4), .B(B4), .I__lt(C5_o__lt), .I__eq(C5_o__eq), .I__gt(C5_o__gt), .O__lt(C4_o__lt), .O__eq(C4_o__eq),
    .O__gt(C4_o__gt));
  full_comparator_1bit C5 (
    .A(A5), .B(B5), .I__lt(C6_o__lt), .I__eq(C6_o__eq), .I__gt(C6_o__gt), .O__lt(C5_o__lt), .O__eq(C5_o__eq),
    .O__gt(C5_o__gt));
  full_comparator_1bit C6 (
    .A(A6), .B(B6), .I__lt(half_comparator_1bit_1_o__lt), .I__eq(half_comparator_1bit_1_o__eq),
    .I__gt(half_comparator_1bit_1_o__gt), .O__lt(C6_o__lt), .O__eq(C6_o__eq), .O__gt(C6_o__gt));
  half_comparator_1bit half_comparator_1bit_1 (
    .A(A7), .B(B7), .O__lt(half_comparator_1bit_1_o__lt), .O__eq(half_comparator_1bit_1_o__eq),
    .O__gt(half_comparator_1bit_1_o__gt));

  // Notes on the sheet:
  //   A__gt__B: A > B
endmodule
