// Digital circuit full_adder_circuits.dig as structural Verilog
module full_adder_circuits (
  input  A,
  input  B,
  input  Cin,
  input  A0,
  input  B0,
  input  Cin0,
  input  A1,
  input  B1,
  input  Cin1,
  input  A2,
  input  B2,
  input  Cin2,
  input  A3,
  input  B3,
  input  Cin3,
  input  A4,
  input  B4,
  input  Cin4,
  input  A5,
  input  B5,
  input  Cin5,
  input  A6,
  input  B6,
  input  Cin6,
  input  A7,
  input  B7,
  input  Cin7,
  output Sum,
  output Cout
);

  wire and_1_out, and_2_out, and_3_out, and_4_out, and_5_out, and_6_out, and_7_out, and_8_out, and_9_out,
       and_10_out, and_11_out, and_12_out, and_13_out, and_14_out, and_15_out, and_16_out, and_17_out,
       and_18_out, and_19_out, and_20_out, and_21_out, and_22_out, and_23_out, and_24_out, and_25_out,
       and_26_out, and_27_out, and_28_out, and_29_out, and_30_out, and_31_out, not_1_out, not_2_out,
       not_3_out, xor_1_out, xor_3_out, xor_5_out, xor_7_out, xor_9_out, xor_11_out, xor_13_out, xor_15_out;

  not not_1 (not_1_out, A);
  not not_2 (not_2_out, B);
  not not_3 (not_3_out, Cin);
  and and_1 (and_1_out, not_1_out, not_2_out, Cin);
  and and_2 (and_2_out, not_1_out, B, not_3_out);
  and and_3 (and_3_out, A, not_2_out, not_3_out);
  and and_4 (and_4_out, Cin, B, A);
  and and_5 (and_5_out, B, Cin);
  and and_6 (and_6_out, A, Cin);
  and and_7 (and_7_out, B, A);
  or or_1 (Sum, and_1_out, and_2_out, and_3_out, and_4_out);
  or or_2 (Cout, and_5_out, and_6_out, and_7_out);
  xor xor_1 (xor_1_out, A0, B0);
  and and_8 (and_8_out, Cin0, A0);
  and and_9 (and_9_out, Cin0, B0);
  and and_10 (and_10_out, B0, A0);
  // XOr xor_2 has open pins: In_1=xor_1_out, In_2=Cin0, out=open
  // Or or_3 has open pins: In_1=and_8_out, In_2=and_9_out, In_3=and_10_out, out=open
  xor xor_3 (xor_3_out, A1, B1);
  and and_11 (and_11_out, Cin1, A1);
  and and_12 (and_12_out, Cin1, B1);
  and and_13 (and_13_out, B1, A1);
  // XOr xor_4 has open pins: In_1=xor_3_out, In_2=Cin1, out=open
  or or_4 (Cin0, and_11_out, and_12_out, and_13_out);
  xor xor_5 (xor_5_out, A2, B2);
  and and_14 (and_14_out, Cin2, A2);
  and and_15 (and_15_out, Cin2, B2);
  and and_16 (and_16_out, B2, A2);
  // XOr xor_6 has open pins: In_1=xor_5_out, In_2=Cin2, out=open
  or or_5 (Cin1, and_14_out, and_15_out, and_16_out);
  xor xor_7 (xor_7_out, A3, B3);
  and and_17 (and_17_out, Cin3, A3);
  and and_18 (and_18_out, Cin3, B3);
  and and_19 (and_19_out, B3, A3);
  // XOr xor_8 has open pins: In_1=xor_7_out, In_2=Cin3, out=open
  or or_6 (Cin2, and_17_out, and_18_out, and_19_out);
  xor xor_9 (xor_9_out, A4, B4);
  and and_20 (and_20_out, Cin4, A4);
  and and_21 (and_21_out, Cin4, B4);
  and and_22 (and_22_out, B4, A4);
  // XOr xor_10 has open pins: In_1=xor_9_out, In_2=Cin4, out=open
  or or_7 (Cin3, and_20_out, and_21_out, and_22_out);
  xor xor_11 (xor_11_out, A5, B5);
  and and_23 (and_23_out, Cin5, A5);
  and and_24 (and_24_out, Cin5, B5);
  and and_25 (and_25_out, B5, A5);
  // XOr xor_12 has open pins: In_1=xor_11_out, In_2=Cin5, out=open
  or or_8 (Cin4, and_23_out, and_24_out, and_25_out);
  xor xor_13 (xor_13_out, A6, B6);
  and and_26 (and_26_out, Cin6, A6);
  and and_27 (and_27_out, Cin6, B6);
  and and_28 (and_28_out, B6, A6);
  // XOr xor_14 has open pins: In_1=xor_13_out, In_2=Cin6, out=open
  or or_9 (Cin5, and_26_out, and_27_out, and_28_out);
  xor xor_15 (xor_15_out, A7, B7);
  and and_29 (and_29_out, Cin7, A7);
  and and_30 (and_30_out, Cin7, B7);
  and and_31 (and_31_out, B7, A7);
  // XOr xor_16 has open pins: In_1=xor_15_out, In_2=Cin7, out=open
  or or_10 (Cin6, and_29_out, and_30_out, and_31_out);
endmodule
