// Digital circuit full_subtractor_1bit.dig as structural Verilog
module full_subtractor_1bit (
  input  A,
  input  B,
  input  Borrow_In,
  output Borrow_Out,
  output Diff
);

  wire and_1_out, and_2_out, not_1_out, not_2_out, xor_1_out;

  not not_1 (not_1_out, A);
  xor xor_1 (xor_1_out, A, B);
  and and_1 (and_1_out, B, not_1_out);
  not not_2 (not_2_out, xor_1_out);
  xor xor_2 (Diff, xor_1_out, Borrow_In);
  and and_2 (and_2_out, Borrow_In, not_2_out);
  and and_3 (Borrow_Out, and_2_out, and_1_out);
endmodule
