// Digital circuit half_comparator_1bit.dig as structural Verilog
module half_comparator_1bit (
  input  A,
  input  B,
  output O__lt,
  output O__eq,
  output O__gt
);

  wire not_1_out, not_2_out;

  not not_1 (not_1_out, A);
  not not_2 (not_2_out, B);
  and and_1 (O__lt, not_1_out, B);
  xnor xnor_1 (O__eq, A, B);
  and and_2 (O__gt, A, not_2_out);
endmodule
