// Digital circuit subtractor_8bit.dig as structural Verilog
module subtractor_8bit (
  input  A,
  input  B,
  input  Borrow_In,
  input  A_2,
  input  B_2,
  input  Borrow_In_2,
  input  A_3,
  input  B_3,
  input  Borrow_In_3,
  input  A_4,
  input  B_4,
  input  Borrow_In_4,
  input  A_5,
  input  B_5,
  input  Borrow_In_5,
  input  A_6,
  input  B_6,
  input  Borrow_In_6,
  input  A_7,
  input  B_7,
  input  Borrow_In_7,
  input  A_8,
  input  B_8,
  input  Borrow_In_8,
  output Borrow_Out,
  output Diff,
  output Borrow_Out_2,
  output Diff_2,
  output Borrow_Out_3,
  output Diff_3,
  output Borrow_Out_4,
  output Diff_4,
  output Borrow_Out_5,
  output Diff_5,
  output Borrow_Out_6,
  output Diff_6,
  output Borrow_Out_7,
  output Diff_7,
  output Borrow_Out_8,
  output Diff_8
);

  wire and_1_out, and_2_out, and_3_out, and_4_out, and_5_out, and_6_out, and_7_out, and_8_out, and_9_out,
       and_10_out, and_11_out, and_12_out, and_13_out, and_14_out, and_15_out, and_16_out, not_1_out,
       not_2_out, not_3_out, not_4_out, not_5_out, not_6_out, not_7_out, not_8_out, not_9_out, not_10_out,
       not_11_out, not_12_out, not_13_out, not_14_out, not_15_out, not_16_out, xor_1_out, xor_2_out,
       xor_3_out, xor_4_out, xor_5_out, xor_6_out, xor_7_out, xor_8_out;

  not not_1 (not_1_out, A);
  xor xor_1 (xor_1_out, A, B);
  and and_1 (and_1_out, B, not_1_out);
  not not_2 (not_2_out, A_2);
  not not_3 (not_3_out, A_3);
  not not_4 (not_4_out, A_4);
  not not_5 (not_5_out, A_5);
  not not_6 (not_6_out, A_6);
  not not_7 (not_7_out, A_7);
  not not_8 (not_8_out, A_8);
  xor xor_2 (xor_2_out, A_2, B_2);
  and and_2 (and_2_out, B_2, not_2_out);
  xor xor_3 (xor_3_out, A_3, B_3);
  and and_3 (and_3_out, B_3, not_3_out);
  xor xor_4 (xor_4_out, A_4, B_4);
  and and_4 (and_4_out, B_4, not_4_out);
  xor xor_5 (xor_5_out, A_5, B_5);
  and and_5 (and_5_out, B_5, not_5_out);
  xor xor_6 (xor_6_out, A_6, B_6);
  and and_6 (and_6_out, B_6, not_6_out);
  xor xor_7 (xor_7_out, A_7, B_7);
  and and_7 (and_7_out, B_7, not_7_out);
  xor xor_8 (xor_8_out, A_8, B_8);
  and and_8 (and_8_out, B_8, not_8_out);
  not not_9 (not_9_out, xor_1_out);
  not not_10 (not_10_out, xor_2_out);
  not not_11 (not_11_out, xor_3_out);
  not not_12 (not_12_out, xor_4_out);
  not not_13 (not_13_out, xor_5_out);
  not not_14 (not_14_out, xor_6_out);
  not not_15 (not_15_out, xor_7_out);
  not not_16 (not_16_out, xor_8_out);
  xor xor_9 (Diff, xor_1_out, Borrow_In);
  and and_9 (and_9_out, Borrow_In, not_9_out);
  xor xor_10 (Diff_2, xor_2_out, Borrow_In_2);
  and and_10 (and_10_out, Borrow_In_2, not_10_out);
  xor xor_11 (Diff_3, xor_3_out, Borrow_In_3);
  and and_11 (and_11_out, Borrow_In_3, not_11_out);
  xor xor_12 (Diff_4, xor_4_out, Borrow_In_4);
  and and_12 (and_12_out, Borrow_In_4, not_12_out);
  xor xor_13 (Diff_5, xor_5_out, Borrow_In_5);
  and and_13 (and_13_out, Borrow_In_5, not_13_out);
  xor xor_14 (Diff_6, xor_6_out, Borrow_In_6);
  and and_14 (and_14_out, Borrow_In_6, not_14_out);
  xor xor_15 (Diff_7, xor_7_out, Borrow_In_7);
  and and_15 (and_15_out, Borrow_In_7, not_15_out);
  xor xor_16 (Diff_8, xor_8_out, Borrow_In_8);
  and and_16 (and_16_out, Borrow_In_8, not_16_out);
  and and_17 (Borrow_In_2, and_9_out, and_1_out);
  and and_18 (Borrow_In_3, and_10_out, and_2_out);
  and and_19 (Borrow_In_4, and_11_out, and_3_out);
  and and_20 (Borrow_In_5, and_12_out, and_4_out);
  and and_21 (Borrow_In_6, and_13_out, and_5_out);
  and and_22 (Borrow_Out_6, and_14_out, and_6_out);
  and and_23 (Borrow_Out_7, and_15_out, and_7_out);
  and and_24 (Borrow_Out_8, and_16_out, and_8_out);

  assign Borrow_Out = Borrow_In_2;
  assign Borrow_Out_2 = Borrow_In_3;
  assign Borrow_Out_3 = Borrow_In_4;
  assign Borrow_Out_4 = Borrow_In_5;
  assign Borrow_Out_5 = Borrow_In_6;
endmodule
